// Logisim project PPUPlayer.circ as structural Verilog: 5 circuits, main circuit PPUPlayer_All
module PPUPlayer_All (
  input  R_W,
  input  [7:0] DB,
  input  [2:0] RS,
  input  nDBE,
  input  nRES
);

  wire CLK_out, n2c02_ntsc_1_ale, n2c02_ntsc_1_nrd, n2c02_ntsc_1_nwr, not_1_out, not_2_out,
       nrom_cartridge_1_nvram_cs, pull_resistor_1_node, videodumper_1_we;
  wire [5:0] n2c02_ntsc_1_pa8;
  wire [7:0] ls373_1_val_out, n2c02_ntsc_1_pa0, n2c02_ntsc_1_pd0_w, nrom_cartridge_1_ppudata_out;
  wire [10:10] nrom_cartridge_1_vram_a10;
  wire [15:0] n2c02_ntsc_1_raw_out, videodumper_1_data;
  wire [23:0] videodumper_1_addr;

  Clock CLK (.out(CLK_out));
  Pull_Resistor #(.pull(1)) pull_resistor_1 (.node(pull_resistor_1_node));
  _2C02_NTSC u_2c02_ntsc_1 (
    .nRES(nRES), .nINT(pull_resistor_1_node), .RS2(RS[2]), .RS1(RS[1]), .RS0(RS[0]), .R_W(R_W), .D7(DB[7]),
    .D6(DB[6]), .D5(DB[5]), .D4(DB[4]), .D3(DB[3]), .D2(DB[2]), .D1(DB[1]), .D0(DB[0]),
    .nRD(n2c02_ntsc_1_nrd), .nWR(n2c02_ntsc_1_nwr), .PA13(n2c02_ntsc_1_pa8[5]), .PA12(n2c02_ntsc_1_pa8[4]),
    .PA11(n2c02_ntsc_1_pa8[3]), .PA10(n2c02_ntsc_1_pa8[2]), .PA9(n2c02_ntsc_1_pa8[1]),
    .PA8(n2c02_ntsc_1_pa8[0]), .PA7(n2c02_ntsc_1_pa0[7]), .PA6(n2c02_ntsc_1_pa0[6]),
    .PA5(n2c02_ntsc_1_pa0[5]), .PA4(n2c02_ntsc_1_pa0[4]), .PA3(n2c02_ntsc_1_pa0[3]),
    .PA2(n2c02_ntsc_1_pa0[2]), .PA1(n2c02_ntsc_1_pa0[1]), .PA0(n2c02_ntsc_1_pa0[0]), .ALE(n2c02_ntsc_1_ale),
    .PD7(nrom_cartridge_1_ppudata_out[7]), .PD6(nrom_cartridge_1_ppudata_out[6]),
    .PD5(nrom_cartridge_1_ppudata_out[5]), .PD4(nrom_cartridge_1_ppudata_out[4]),
    .PD3(nrom_cartridge_1_ppudata_out[3]), .PD2(nrom_cartridge_1_ppudata_out[2]),
    .PD1(nrom_cartridge_1_ppudata_out[1]), .PD0(nrom_cartridge_1_ppudata_out[0]),
    .PD7_W(n2c02_ntsc_1_pd0_w[7]), .PD6_W(n2c02_ntsc_1_pd0_w[6]), .PD5_W(n2c02_ntsc_1_pd0_w[5]),
    .PD4_W(n2c02_ntsc_1_pd0_w[4]), .PD3_W(n2c02_ntsc_1_pd0_w[3]), .PD2_W(n2c02_ntsc_1_pd0_w[2]),
    .PD1_W(n2c02_ntsc_1_pd0_w[1]), .PD0_W(n2c02_ntsc_1_pd0_w[0]), .EXT0(1'b0), .EXT1(1'b0), .EXT2(1'b0),
    .EXT3(1'b0), .CLK(CLK_out), .nDBE(nDBE), .DbgRenderEnable(1'b1), .RAW_OUT(n2c02_ntsc_1_raw_out));  // open: VOUT, D7_2, D6_2, D5_2, D4_2, D3_2, D2_2, D1_2, D0_2, EXT0_2, EXT1_2, EXT2_2, EXT3_2
  not not_1 (not_1_out, pull_resistor_1_node);
  LED led_1 (.in(not_1_out));
  VideoDumper videodumper_1 (
    .CLK(CLK_out), .RAW(n2c02_ntsc_1_raw_out), .ADDR(videodumper_1_addr), .DATA(videodumper_1_data),
    .WE(videodumper_1_we));
  LS373 ls373_1 (.LE(n2c02_ntsc_1_ale), .nOE(1'b0), .val_in(n2c02_ntsc_1_pa0), .val_out(ls373_1_val_out));
  RAM #(.addrWidth(24), .dataWidth(16), .bus("separate")) ram_1 (
    .addr(videodumper_1_addr), .din(videodumper_1_data), .str(videodumper_1_we), .sel(1'b1),
    .clk(videodumper_1_we), .ld(1'b0), .clr(1'b0));  // open: data
  NROM_Cartridge nrom_cartridge_1 (
    .PPUData_In(n2c02_ntsc_1_pd0_w), .nRD(n2c02_ntsc_1_nrd), .nWR(n2c02_ntsc_1_nwr),
    .PPUAddr({n2c02_ntsc_1_pa8, ls373_1_val_out}), .nPA13(not_2_out),
    .PPUData_Out(nrom_cartridge_1_ppudata_out), .nVRAM_CS(nrom_cartridge_1_nvram_cs),
    .VRAM_A10(nrom_cartridge_1_vram_a10[10]), .V_Mirroring(1'b1));
  not not_2 (not_2_out, n2c02_ntsc_1_pa8[5]);
  SRAM sram_1 (
    .nCS(nrom_cartridge_1_nvram_cs), .nWE(n2c02_ntsc_1_nwr), .nOE(n2c02_ntsc_1_nrd),
    .Addr({nrom_cartridge_1_vram_a10[10], n2c02_ntsc_1_pa8[1:0], ls373_1_val_out}),
    .Data_In(n2c02_ntsc_1_pd0_w), .Data_Out(nrom_cartridge_1_ppudata_out));

  // Notes on the sheet:
  //   PA0-7
  //   PPU Data Out
  //   PPU Data In
endmodule

module SRAM (
  input  nCS,
  input  nWE,
  input  nOE,
  input  [10:0] Addr,
  input  [7:0] Data_In,
  output [7:0] Data_Out
);

  wire not_1_out, not_2_out, not_3_out;

  not not_1 (not_1_out, nCS);
  not not_2 (not_2_out, nWE);
  not not_3 (not_3_out, nOE);
  RAM #(.addrWidth(11), .bus("separate")) ram_1 (
    .addr(Addr), .din(Data_In), .data(Data_Out), .str(not_2_out), .sel(not_1_out), .clk(not_1_out),
    .ld(not_3_out));  // open: clr
endmodule

module LS373 (
  input  LE,
  input  nOE,
  input  [7:0] val_in,
  output [7:0] val_out
);

  wire not_1_out;
  wire [7:0] register_1_q;

  not not_1 (not_1_out, nOE);
  Register #(.trigger("high")) register_1 (.D(val_in), .en(LE), .Q(register_1_q), .clk(LE));  // open: clr
  assign val_out = not_1_out ? register_1_q : 8'bz;  // Controlled_Buffer controlled_buffer_1
endmodule

module NROM_Cartridge (
  input  [7:0] PPUData_In,
  input  nRD,
  input  nWR,
  input  [13:0] PPUAddr,
  input  nPA13,
  input  V_Mirroring,
  output [7:0] PPUData_Out,
  output nVRAM_CS,
  output VRAM_A10
);

  wire nor_1_out;

  nor nor_1 (nor_1_out, nRD, PPUAddr[13]);
  ROM #(.addrWidth(13)) rom_1 (.addr(PPUAddr[12:0]), .data(PPUData_Out), .sel(nor_1_out));
  Multiplexer #(.enable("false")) multiplexer_1 (
    .in0(PPUAddr[11]), .in1(PPUAddr[10]), .out(VRAM_A10), .sel(V_Mirroring));

  assign nVRAM_CS = nPA13;

  // Notes on the sheet:
  //   N.C.
  //   N.C.
  //   1: V-Mirroring, 0: H-Mirroring
  //   Simple NROM cartridge (without PRG)
  //   CHR-ROM (0x2000 bytes)
endmodule

module VideoDumper (
  input  CLK,
  input  [15:0] RAW,
  output [23:0] ADDR,
  output [15:0] DATA,
  output WE
);

  Counter #(.width(24), .max('hffffff)) counter_1 (.Q(ADDR), .clk(CLK));  // open: load, D, count, carry, clr

  assign DATA = RAW;
  assign WE = CLK;
endmodule
